// Digital circuit alu_ponderada.dig as structural Verilog
module alu_ponderada (
  input  [7:0] A,
  input  [7:0] B,
  input  [2:0] OP,
  input  L_R,
  output overflow
);

  wire comparacao_8bit_1_a_eq_b, comparacao_8bit_1_a_maior_que_b, comparacao_8bit_1_a_menor_que_b,
       notconnected_1_out, notconnected_2_out, seletor_op_1_comparacao, seletor_op_1_multiplicador,
       seletor_op_1_shift, seletor_op_1_soma, seletor_op_1_subtracao;
  wire [7:0] and_1_out, and_2_out, and_3_out, and_4_out, and_5_out, bitextender_1_out, bitextender_2_out,
       bitextender_3_out, bitextender_4_out, bitextender_5_out, comparacao_manipulador_1_o,
       multiplicador_1_m, or_1_out, shift_1_o, somador_8bit_1_s_2;

  somador_8bit somador_8bit_1 (.S(seletor_op_1_subtracao), .A(A), .B(B), .O(overflow), .S_2(somador_8bit_1_s_2));
  comparacao_8bit comparacao_8bit_1 (
    .A(A), .B(B), .A_menor_que_B(comparacao_8bit_1_a_menor_que_b), .A_eq_B(comparacao_8bit_1_a_eq_b),
    .A_maior_que_B(comparacao_8bit_1_a_maior_que_b));
  shift shift_1 (.A(A), .L_R(L_R), .O(shift_1_o));
  multiplicador multiplicador_1 (.A(A), .B(B), .M(multiplicador_1_m));
  seletor_op seletor_op_1 (
    .In(OP), .SOMA(seletor_op_1_soma), .SUBTRACAO(seletor_op_1_subtracao),
    .COMPARACAO(seletor_op_1_comparacao), .SHIFT(seletor_op_1_shift),
    .MULTIPLICADOR(seletor_op_1_multiplicador));
  BitExtender #(.inputBits(1), .outputBits(8)) bitextender_1 (.in(seletor_op_1_soma), .out(bitextender_1_out));
  BitExtender #(.inputBits(1), .outputBits(8)) bitextender_2 (.in(seletor_op_1_subtracao), .out(bitextender_2_out));
  BitExtender #(.inputBits(1), .outputBits(8)) bitextender_3 (.in(seletor_op_1_comparacao), .out(bitextender_3_out));
  BitExtender #(.inputBits(1), .outputBits(8)) bitextender_4 (.in(seletor_op_1_shift), .out(bitextender_4_out));
  BitExtender #(.inputBits(1), .outputBits(8)) bitextender_5 (.in(seletor_op_1_multiplicador), .out(bitextender_5_out));
  comparacao_manipulador comparacao_manipulador_1 (
    .A_menor_que_B(comparacao_8bit_1_a_menor_que_b), .A_igual_a_B(comparacao_8bit_1_a_eq_b),
    .A_maior_que_B(comparacao_8bit_1_a_maior_que_b), .O(comparacao_manipulador_1_o));
  assign and_1_out = somador_8bit_1_s_2 & bitextender_1_out;  // And and_1, 8 bits wide
  assign and_2_out = somador_8bit_1_s_2 & bitextender_2_out;  // And and_2, 8 bits wide
  assign and_3_out = comparacao_manipulador_1_o & bitextender_3_out;  // And and_3, 8 bits wide
  assign and_4_out = shift_1_o & bitextender_4_out;  // And and_4, 8 bits wide
  assign and_5_out = multiplicador_1_m & bitextender_5_out;  // And and_5, 8 bits wide
  assign or_1_out = and_1_out | and_2_out | and_3_out | and_4_out | and_5_out;  // Or or_1, 8 bits wide
  Seven_Seg_Hex seven_seg_hex_1 (.d(or_1_out[7:4]), .dp(notconnected_1_out));
  Seven_Seg_Hex seven_seg_hex_2 (.d(or_1_out[3:0]), .dp(notconnected_2_out));
  // NotConnected on notconnected_1_out
  // NotConnected on notconnected_2_out
endmodule
