// Digital circuit comparacao_1bit.dig as structural Verilog
module comparacao_1bit (
  input  A,
  input  B,
  output A_menor_que_B,
  output A_maior_que_B,
  output A_igual_a_B
);

  wire not_1_out, not_2_out;

  not not_1 (not_1_out, A);
  not not_2 (not_2_out, B);
  and and_1 (A_menor_que_B, not_1_out, B);
  and and_2 (A_maior_que_B, A, not_2_out);
  nor nor_1 (A_igual_a_B, A_menor_que_B, A_maior_que_B);
endmodule
