// Digital circuit comparacao_8bit.dig as structural Verilog
module comparacao_8bit (
  input  [7:0] A,
  input  [7:0] B,
  output A_menor_que_B,
  output A_eq_B,
  output A_maior_que_B
);

  wire and_2_out, and_3_out, and_4_out, and_5_out, and_6_out, and_7_out, and_8_out, and_9_out, and_10_out,
       and_11_out, and_12_out, and_13_out, and_14_out, and_15_out, comparacao_1bit_1_a_igual_a_b,
       comparacao_1bit_1_a_maior_que_b, comparacao_1bit_1_a_menor_que_b, comparacao_1bit_2_a_igual_a_b,
       comparacao_1bit_2_a_maior_que_b, comparacao_1bit_2_a_menor_que_b, comparacao_1bit_3_a_igual_a_b,
       comparacao_1bit_3_a_maior_que_b, comparacao_1bit_3_a_menor_que_b, comparacao_1bit_4_a_igual_a_b,
       comparacao_1bit_4_a_maior_que_b, comparacao_1bit_4_a_menor_que_b, comparacao_1bit_5_a_igual_a_b,
       comparacao_1bit_5_a_maior_que_b, comparacao_1bit_5_a_menor_que_b, comparacao_1bit_6_a_igual_a_b,
       comparacao_1bit_6_a_maior_que_b, comparacao_1bit_6_a_menor_que_b, comparacao_1bit_7_a_igual_a_b,
       comparacao_1bit_7_a_maior_que_b, comparacao_1bit_7_a_menor_que_b, comparacao_1bit_8_a_igual_a_b,
       comparacao_1bit_8_a_maior_que_b, comparacao_1bit_8_a_menor_que_b;

  comparacao_1bit comparacao_1bit_1 (
    .A(A[7]), .B(B[7]), .A_menor_que_B(comparacao_1bit_1_a_menor_que_b),
    .A_maior_que_B(comparacao_1bit_1_a_maior_que_b), .A_igual_a_B(comparacao_1bit_1_a_igual_a_b));
  comparacao_1bit comparacao_1bit_2 (
    .A(A[6]), .B(B[6]), .A_menor_que_B(comparacao_1bit_2_a_menor_que_b),
    .A_maior_que_B(comparacao_1bit_2_a_maior_que_b), .A_igual_a_B(comparacao_1bit_2_a_igual_a_b));
  comparacao_1bit comparacao_1bit_3 (
    .A(A[5]), .B(B[5]), .A_menor_que_B(comparacao_1bit_3_a_menor_que_b),
    .A_maior_que_B(comparacao_1bit_3_a_maior_que_b), .A_igual_a_B(comparacao_1bit_3_a_igual_a_b));
  comparacao_1bit comparacao_1bit_4 (
    .A(A[4]), .B(B[4]), .A_menor_que_B(comparacao_1bit_4_a_menor_que_b),
    .A_maior_que_B(comparacao_1bit_4_a_maior_que_b), .A_igual_a_B(comparacao_1bit_4_a_igual_a_b));
  comparacao_1bit comparacao_1bit_5 (
    .A(A[3]), .B(B[3]), .A_menor_que_B(comparacao_1bit_5_a_menor_que_b),
    .A_maior_que_B(comparacao_1bit_5_a_maior_que_b), .A_igual_a_B(comparacao_1bit_5_a_igual_a_b));
  comparacao_1bit comparacao_1bit_6 (
    .A(A[2]), .B(B[2]), .A_menor_que_B(comparacao_1bit_6_a_menor_que_b),
    .A_maior_que_B(comparacao_1bit_6_a_maior_que_b), .A_igual_a_B(comparacao_1bit_6_a_igual_a_b));
  comparacao_1bit comparacao_1bit_7 (
    .A(A[1]), .B(B[1]), .A_menor_que_B(comparacao_1bit_7_a_menor_que_b),
    .A_maior_que_B(comparacao_1bit_7_a_maior_que_b), .A_igual_a_B(comparacao_1bit_7_a_igual_a_b));
  comparacao_1bit comparacao_1bit_8 (
    .A(A[0]), .B(B[0]), .A_menor_que_B(comparacao_1bit_8_a_menor_que_b),
    .A_maior_que_B(comparacao_1bit_8_a_maior_que_b), .A_igual_a_B(comparacao_1bit_8_a_igual_a_b));
  and and_1 (A_eq_B, comparacao_1bit_1_a_igual_a_b, comparacao_1bit_2_a_igual_a_b, comparacao_1bit_3_a_igual_a_b, comparacao_1bit_4_a_igual_a_b, comparacao_1bit_5_a_igual_a_b, comparacao_1bit_6_a_igual_a_b, comparacao_1bit_7_a_igual_a_b, comparacao_1bit_8_a_igual_a_b);
  and and_2 (and_2_out, comparacao_1bit_8_a_maior_que_b, comparacao_1bit_7_a_igual_a_b, comparacao_1bit_6_a_igual_a_b, comparacao_1bit_5_a_igual_a_b, comparacao_1bit_4_a_igual_a_b, comparacao_1bit_3_a_igual_a_b, comparacao_1bit_2_a_igual_a_b, comparacao_1bit_1_a_igual_a_b);
  and and_3 (and_3_out, comparacao_1bit_7_a_maior_que_b, comparacao_1bit_6_a_igual_a_b, comparacao_1bit_5_a_igual_a_b, comparacao_1bit_4_a_igual_a_b, comparacao_1bit_3_a_igual_a_b, comparacao_1bit_2_a_igual_a_b, comparacao_1bit_1_a_igual_a_b);
  and and_4 (and_4_out, comparacao_1bit_6_a_maior_que_b, comparacao_1bit_5_a_igual_a_b, comparacao_1bit_4_a_igual_a_b, comparacao_1bit_3_a_igual_a_b, comparacao_1bit_2_a_igual_a_b, comparacao_1bit_1_a_igual_a_b);
  and and_5 (and_5_out, comparacao_1bit_5_a_maior_que_b, comparacao_1bit_4_a_igual_a_b, comparacao_1bit_3_a_igual_a_b, comparacao_1bit_2_a_igual_a_b, comparacao_1bit_1_a_igual_a_b);
  and and_6 (and_6_out, comparacao_1bit_4_a_maior_que_b, comparacao_1bit_3_a_igual_a_b, comparacao_1bit_2_a_igual_a_b, comparacao_1bit_1_a_igual_a_b);
  and and_7 (and_7_out, comparacao_1bit_3_a_maior_que_b, comparacao_1bit_2_a_igual_a_b, comparacao_1bit_1_a_igual_a_b);
  and and_8 (and_8_out, comparacao_1bit_2_a_maior_que_b, comparacao_1bit_1_a_igual_a_b);
  and and_9 (and_9_out, comparacao_1bit_1_a_igual_a_b, comparacao_1bit_2_a_menor_que_b);
  and and_10 (and_10_out, comparacao_1bit_1_a_igual_a_b, comparacao_1bit_2_a_igual_a_b, comparacao_1bit_3_a_menor_que_b);
  and and_11 (and_11_out, comparacao_1bit_1_a_igual_a_b, comparacao_1bit_2_a_igual_a_b, comparacao_1bit_3_a_igual_a_b, comparacao_1bit_4_a_menor_que_b);
  and and_12 (and_12_out, comparacao_1bit_1_a_igual_a_b, comparacao_1bit_2_a_igual_a_b, comparacao_1bit_3_a_igual_a_b, comparacao_1bit_4_a_igual_a_b, comparacao_1bit_5_a_menor_que_b);
  and and_13 (and_13_out, comparacao_1bit_1_a_igual_a_b, comparacao_1bit_2_a_igual_a_b, comparacao_1bit_3_a_igual_a_b, comparacao_1bit_4_a_igual_a_b, comparacao_1bit_5_a_igual_a_b, comparacao_1bit_6_a_menor_que_b);
  and and_14 (and_14_out, comparacao_1bit_1_a_igual_a_b, comparacao_1bit_2_a_igual_a_b, comparacao_1bit_3_a_igual_a_b, comparacao_1bit_4_a_igual_a_b, comparacao_1bit_5_a_igual_a_b, comparacao_1bit_6_a_igual_a_b, comparacao_1bit_7_a_menor_que_b);
  and and_15 (and_15_out, comparacao_1bit_1_a_igual_a_b, comparacao_1bit_2_a_igual_a_b, comparacao_1bit_3_a_igual_a_b, comparacao_1bit_4_a_igual_a_b, comparacao_1bit_5_a_igual_a_b, comparacao_1bit_6_a_igual_a_b, comparacao_1bit_7_a_igual_a_b, comparacao_1bit_8_a_menor_que_b);
  xor xor_1 (A_maior_que_B, and_2_out, and_3_out, and_4_out, and_5_out, and_6_out, and_7_out, and_8_out, comparacao_1bit_1_a_maior_que_b);
  xor xor_2 (A_menor_que_B, comparacao_1bit_1_a_menor_que_b, and_9_out, and_10_out, and_11_out, and_12_out, and_13_out, and_14_out, and_15_out);
endmodule
