// Digital circuit multiplicador.dig as structural Verilog
module multiplicador (
  input  [7:0] A,
  input  [7:0] B,
  output [7:0] M
);

  wire [7:0] seletor_1_a0, seletor_1_a1, seletor_1_a2, seletor_1_a3, seletor_1_a4, seletor_1_a5,
       seletor_1_a6, seletor_1_a7, shift_1_o, shift_2_o, shift_3_o, shift_4_o, shift_5_o, shift_6_o,
       shift_7_o, shift_8_o, shift_9_o, shift_10_o, shift_11_o, shift_12_o, shift_13_o, shift_14_o,
       shift_15_o, shift_16_o, shift_17_o, shift_18_o, shift_19_o, shift_20_o, shift_21_o, shift_22_o,
       shift_23_o, shift_24_o, shift_25_o, shift_26_o, shift_27_o, shift_28_o, somador_8bit_1_s_2,
       somador_8bit_2_s_2, somador_8bit_3_s_2, somador_8bit_4_s_2, somador_8bit_5_s_2, somador_8bit_6_s_2;

  seletor seletor_1 (
    .A(A), .B(B), .A0(seletor_1_a0), .A1(seletor_1_a1), .A2(seletor_1_a2), .A3(seletor_1_a3),
    .A4(seletor_1_a4), .A5(seletor_1_a5), .A6(seletor_1_a6), .A7(seletor_1_a7));
  shift shift_1 (.A(seletor_1_a1), .L_R(1'b0), .O(shift_1_o));
  shift shift_2 (.A(seletor_1_a2), .L_R(1'b0), .O(shift_2_o));
  shift shift_3 (.A(seletor_1_a3), .L_R(1'b0), .O(shift_3_o));
  shift shift_4 (.A(seletor_1_a4), .L_R(1'b0), .O(shift_4_o));
  shift shift_5 (.A(seletor_1_a5), .L_R(1'b0), .O(shift_5_o));
  shift shift_6 (.A(seletor_1_a6), .L_R(1'b0), .O(shift_6_o));
  shift shift_7 (.A(seletor_1_a7), .L_R(1'b0), .O(shift_7_o));
  somador_8bit somador_8bit_1 (.S(1'b0), .A(seletor_1_a0), .B(shift_1_o), .S_2(somador_8bit_1_s_2));  // open: O
  shift shift_8 (.A(shift_2_o), .L_R(1'b0), .O(shift_8_o));
  shift shift_9 (.A(shift_3_o), .L_R(1'b0), .O(shift_9_o));
  shift shift_10 (.A(shift_4_o), .L_R(1'b0), .O(shift_10_o));
  shift shift_11 (.A(shift_5_o), .L_R(1'b0), .O(shift_11_o));
  shift shift_12 (.A(shift_6_o), .L_R(1'b0), .O(shift_12_o));
  shift shift_13 (.A(shift_7_o), .L_R(1'b0), .O(shift_13_o));
  shift shift_14 (.A(shift_9_o), .L_R(1'b0), .O(shift_14_o));
  shift shift_15 (.A(shift_10_o), .L_R(1'b0), .O(shift_15_o));
  shift shift_16 (.A(shift_11_o), .L_R(1'b0), .O(shift_16_o));
  shift shift_17 (.A(shift_12_o), .L_R(1'b0), .O(shift_17_o));
  shift shift_18 (.A(shift_13_o), .L_R(1'b0), .O(shift_18_o));
  somador_8bit somador_8bit_2 (.S(1'b0), .A(shift_8_o), .B(shift_14_o), .S_2(somador_8bit_2_s_2));  // open: O
  shift shift_19 (.A(shift_15_o), .L_R(1'b0), .O(shift_19_o));
  shift shift_20 (.A(shift_16_o), .L_R(1'b0), .O(shift_20_o));
  shift shift_21 (.A(shift_17_o), .L_R(1'b0), .O(shift_21_o));
  shift shift_22 (.A(shift_18_o), .L_R(1'b0), .O(shift_22_o));
  somador_8bit somador_8bit_3 (
    .S(1'b0), .A(somador_8bit_1_s_2), .B(somador_8bit_2_s_2), .S_2(somador_8bit_3_s_2));  // open: O
  shift shift_23 (.A(shift_20_o), .L_R(1'b0), .O(shift_23_o));
  shift shift_24 (.A(shift_21_o), .L_R(1'b0), .O(shift_24_o));
  shift shift_25 (.A(shift_22_o), .L_R(1'b0), .O(shift_25_o));
  somador_8bit somador_8bit_4 (.S(1'b0), .A(shift_19_o), .B(shift_23_o), .S_2(somador_8bit_4_s_2));  // open: O
  shift shift_26 (.A(shift_24_o), .L_R(1'b0), .O(shift_26_o));
  shift shift_27 (.A(shift_25_o), .L_R(1'b0), .O(shift_27_o));
  shift shift_28 (.A(shift_27_o), .L_R(1'b0), .O(shift_28_o));
  somador_8bit somador_8bit_5 (.S(1'b0), .A(shift_26_o), .B(shift_28_o), .S_2(somador_8bit_5_s_2));  // open: O
  somador_8bit somador_8bit_6 (
    .S(1'b0), .A(somador_8bit_4_s_2), .B(somador_8bit_5_s_2), .S_2(somador_8bit_6_s_2));  // open: O
  somador_8bit somador_8bit_7 (.S(1'b0), .A(somador_8bit_3_s_2), .B(somador_8bit_6_s_2), .S_2(M));  // open: O
endmodule
