// Digital circuit right_bit_shift.dig as structural Verilog
module right_bit_shift (
  input  [7:0] A,
  input  _1_bit,
  input  _2_bit,
  input  _4_bit,
  output [7:0] O
);

  wire multiplexer_1_out, multiplexer_2_out, multiplexer_3_out, multiplexer_4_out, multiplexer_5_out,
       multiplexer_6_out, multiplexer_7_out, multiplexer_8_out, multiplexer_9_out, multiplexer_10_out,
       multiplexer_11_out, multiplexer_12_out, multiplexer_13_out, multiplexer_14_out, multiplexer_15_out,
       multiplexer_16_out;

  Multiplexer multiplexer_1 (.sel(_1_bit), .in_0(A[0]), .in_1(A[1]), .out(multiplexer_1_out));
  Multiplexer multiplexer_2 (.sel(_1_bit), .in_0(A[1]), .in_1(A[2]), .out(multiplexer_2_out));
  Multiplexer multiplexer_3 (.sel(_1_bit), .in_0(A[2]), .in_1(A[3]), .out(multiplexer_3_out));
  Multiplexer multiplexer_4 (.sel(_1_bit), .in_0(A[3]), .in_1(A[4]), .out(multiplexer_4_out));
  Multiplexer multiplexer_5 (.sel(_1_bit), .in_0(A[4]), .in_1(A[5]), .out(multiplexer_5_out));
  Multiplexer multiplexer_6 (.sel(_1_bit), .in_0(A[5]), .in_1(A[6]), .out(multiplexer_6_out));
  Multiplexer multiplexer_7 (.sel(_1_bit), .in_0(A[6]), .in_1(A[7]), .out(multiplexer_7_out));
  Multiplexer multiplexer_8 (.sel(_1_bit), .in_0(A[7]), .in_1(1'b0), .out(multiplexer_8_out));
  Multiplexer multiplexer_9 (.sel(_2_bit), .in_0(multiplexer_1_out), .in_1(multiplexer_3_out), .out(multiplexer_9_out));
  Multiplexer multiplexer_10 (
    .sel(_2_bit), .in_0(multiplexer_2_out), .in_1(multiplexer_4_out), .out(multiplexer_10_out));
  Multiplexer multiplexer_11 (
    .sel(_2_bit), .in_0(multiplexer_3_out), .in_1(multiplexer_5_out), .out(multiplexer_11_out));
  Multiplexer multiplexer_12 (
    .sel(_2_bit), .in_0(multiplexer_4_out), .in_1(multiplexer_6_out), .out(multiplexer_12_out));
  Multiplexer multiplexer_13 (
    .sel(_2_bit), .in_0(multiplexer_5_out), .in_1(multiplexer_7_out), .out(multiplexer_13_out));
  Multiplexer multiplexer_14 (
    .sel(_2_bit), .in_0(multiplexer_6_out), .in_1(multiplexer_8_out), .out(multiplexer_14_out));
  Multiplexer multiplexer_15 (.sel(_2_bit), .in_0(multiplexer_7_out), .in_1(1'b0), .out(multiplexer_15_out));
  Multiplexer multiplexer_16 (.sel(_2_bit), .in_0(multiplexer_8_out), .in_1(1'b0), .out(multiplexer_16_out));
  Multiplexer multiplexer_17 (.sel(_4_bit), .in_0(multiplexer_9_out), .in_1(multiplexer_13_out), .out(O[0]));
  Multiplexer multiplexer_18 (.sel(_4_bit), .in_0(multiplexer_10_out), .in_1(multiplexer_14_out), .out(O[1]));
  Multiplexer multiplexer_19 (.sel(_4_bit), .in_0(multiplexer_11_out), .in_1(multiplexer_15_out), .out(O[2]));
  Multiplexer multiplexer_20 (.sel(_4_bit), .in_0(multiplexer_12_out), .in_1(multiplexer_16_out), .out(O[3]));
  Multiplexer multiplexer_21 (.sel(_4_bit), .in_0(multiplexer_13_out), .in_1(1'b0), .out(O[4]));
  Multiplexer multiplexer_22 (.sel(_4_bit), .in_0(multiplexer_14_out), .in_1(1'b0), .out(O[5]));
  Multiplexer multiplexer_23 (.sel(_4_bit), .in_0(multiplexer_15_out), .in_1(1'b0), .out(O[6]));
  Multiplexer multiplexer_24 (.sel(_4_bit), .in_0(multiplexer_16_out), .in_1(1'b0), .out(O[7]));
endmodule
