// Digital circuit seletor.dig as structural Verilog
module seletor (
  input  [7:0] A,
  input  [7:0] B,
  output [7:0] A0,
  output [7:0] A1,
  output [7:0] A2,
  output [7:0] A3,
  output [7:0] A4,
  output [7:0] A5,
  output [7:0] A6,
  output [7:0] A7
);

  Multiplexer #(.Bits(8)) multiplexer_1 (.sel(B[0]), .in_0({8{1'b0}}), .in_1(A), .out(A0));
  Multiplexer #(.Bits(8)) multiplexer_2 (.sel(B[1]), .in_0({8{1'b0}}), .in_1(A), .out(A1));
  Multiplexer #(.Bits(8)) multiplexer_3 (.sel(B[2]), .in_0({8{1'b0}}), .in_1(A), .out(A2));
  Multiplexer #(.Bits(8)) multiplexer_4 (.sel(B[3]), .in_0({8{1'b0}}), .in_1(A), .out(A3));
  Multiplexer #(.Bits(8)) multiplexer_5 (.sel(B[4]), .in_0({8{1'b0}}), .in_1(A), .out(A4));
  Multiplexer #(.Bits(8)) multiplexer_6 (.sel(B[5]), .in_0({8{1'b0}}), .in_1(A), .out(A5));
  Multiplexer #(.Bits(8)) multiplexer_7 (.sel(B[6]), .in_0({8{1'b0}}), .in_1(A), .out(A6));
  Multiplexer #(.Bits(8)) multiplexer_8 (.sel(B[7]), .in_0({8{1'b0}}), .in_1(A), .out(A7));
endmodule
