// Digital circuit seletor_op.dig as structural Verilog
module seletor_op (
  input  [2:0] In,
  output SOMA,
  output SUBTRACAO,
  output COMPARACAO,
  output SHIFT,
  output MULTIPLICADOR
);

  wire not_1_out, not_2_out, not_3_out;

  not not_1 (not_1_out, In[0]);
  not not_2 (not_2_out, In[1]);
  not not_3 (not_3_out, In[2]);
  and and_1 (SOMA, In[0], not_2_out, not_3_out);
  and and_2 (SUBTRACAO, not_1_out, In[1], not_3_out);
  and and_3 (COMPARACAO, In[0], In[1], not_3_out);
  and and_4 (SHIFT, not_1_out, not_2_out, In[2]);
  and and_5 (MULTIPLICADOR, In[0], not_2_out, In[2]);
endmodule
