// Digital circuit shift.dig as structural Verilog
module shift (
  input  [7:0] A,
  input  L_R,
  output [7:0] O
);

  wire demultiplexer_1_out_0, demultiplexer_1_out_1;
  wire [7:0] left_bit_shift_1_o, right_bit_shift_1_o;

  Demultiplexer demultiplexer_1 (.sel(L_R), .in(1'b1), .out_0(demultiplexer_1_out_0), .out_1(demultiplexer_1_out_1));
  left_bit_shift left_bit_shift_1 (
    .A(A), ._1_bit(demultiplexer_1_out_0), ._2_bit(1'b0), ._4_bit(1'b0), .O(left_bit_shift_1_o));
  right_bit_shift right_bit_shift_1 (
    .A(A), ._1_bit(demultiplexer_1_out_1), ._2_bit(1'b0), ._4_bit(1'b0), .O(right_bit_shift_1_o));
  Multiplexer #(.Bits(8)) multiplexer_1 (.sel(L_R), .in_0(left_bit_shift_1_o), .in_1(right_bit_shift_1_o), .out(O));
endmodule
