// Digital circuit somador_8bit.dig as structural Verilog
module somador_8bit (
  input  S,
  input  [7:0] A,
  input  [7:0] B,
  output O,
  output [7:0] S_2
);

  wire soma_1_c_2, soma_2_c_2, soma_3_c_2, soma_4_c_2, soma_5_c_2, soma_6_c_2, soma_7_c_2, xor_1_out,
       xor_2_out, xor_3_out, xor_4_out, xor_5_out, xor_6_out, xor_7_out, xor_8_out;

  xor xor_1 (xor_1_out, B[0], S);
  xor xor_2 (xor_2_out, B[1], S);
  soma soma_1 (.A(A[0]), .B(xor_1_out), .C(S), .S(S_2[0]), .C_2(soma_1_c_2));
  xor xor_3 (xor_3_out, B[2], S);
  soma soma_2 (.A(A[1]), .B(xor_2_out), .C(soma_1_c_2), .S(S_2[1]), .C_2(soma_2_c_2));
  xor xor_4 (xor_4_out, B[3], S);
  soma soma_3 (.A(A[2]), .B(xor_3_out), .C(soma_2_c_2), .S(S_2[2]), .C_2(soma_3_c_2));
  xor xor_5 (xor_5_out, B[4], S);
  soma soma_4 (.A(A[3]), .B(xor_4_out), .C(soma_3_c_2), .S(S_2[3]), .C_2(soma_4_c_2));
  xor xor_6 (xor_6_out, B[5], S);
  soma soma_5 (.A(A[4]), .B(xor_5_out), .C(soma_4_c_2), .S(S_2[4]), .C_2(soma_5_c_2));
  xor xor_7 (xor_7_out, B[6], S);
  soma soma_6 (.A(A[5]), .B(xor_6_out), .C(soma_5_c_2), .S(S_2[5]), .C_2(soma_6_c_2));
  xor xor_8 (xor_8_out, B[7], S);
  soma soma_7 (.A(A[6]), .B(xor_7_out), .C(soma_6_c_2), .S(S_2[6]), .C_2(soma_7_c_2));
  soma soma_8 (.A(A[7]), .B(xor_8_out), .C(soma_7_c_2), .S(S_2[7]), .C_2(O));
endmodule
